# Fritzing sketch nfc_project (saved by Fritzing 1.0.1rc)

parts:
  Mod1 = Raspberry Pi 4B
  Деталь1 = PN532 Elechouse RFID NFC Module V3 [mn="PN 532 board" mpn=-]
  LCD2 = Waveshare 2.8in TFT touch shield

nets:
  5V: Mod1.5V, Деталь1.VCC, LCD2.pin3, LCD2.pin_29
  GND: Mod1.GND, Деталь1.GND, LCD2.pin4, LCD2.pin_5, LCD2.pin_31
  N1: Mod1.GPIO18, Деталь1.SS
  N2: Mod1.GPIO27, Деталь1.RSTO
  N3: Mod1.GPIO23, LCD2.pin_19
  N4: Mod1.GPIO24, LCD2.pin_21
  N5: Mod1.GPIO10, LCD2.pin_17, LCD2.pin_30
  N6: Mod1.GPIO9, LCD2.pin_16, LCD2.pin_32
  N7: Mod1.GPIO25, LCD2.pin_25
  N8: Mod1.GPIO11, LCD2.pin_15, LCD2.pin_33
  N9: Mod1.GPIO8, LCD2.pin_18
  N10: Mod1.GPIO7, LCD2.pin_24
  N11: Mod1.GPIO19, Деталь1.MISO
  N12: Mod1.GPIO20, Деталь1.MOSI
  N13: Mod1.GPIO21, Деталь1.SCK

custom parts:
  PN532 Elechouse RFID NFC Module V3: NFC is a popular technology in recent years. We often heard this work while smart phone company such as Samsung or HTC introduces their latest high-end phones. Almost all the high-end phone in the market support NFC. Near field communication (NFC) is a set of standards for smart phones and similar devices to establish radio communication with each other by touching them together or bringing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
  Waveshare 2.8in TFT touch shield: This is a generic 2.8 tft spi lcd display. 240×320, Waveshare 2.8inch TFT Touch Shield for Arduino.
